# Fritzing sketch RemoteLCD (saved by Fritzing 0.9.3b)
breadboards: 1

parts:
  U1 = NodeMCU V3.0
  LCD1 = LCD screen
  S1 = Pushbutton [package="[THT]"]
  S2 = Pushbutton [package="[THT]"]
  R1 = Resistor [tolerance=±5% resistance=220 package=THT]
  R2 = Resistor [tolerance=±5% resistance=220 package=THT]
  J1 = Piezo Speaker
  LCM1602_IIC1 = LCM1602 IIC [part_number="LCM1602 IIC" chip_label="LCM1602 IIC" package="DIP (Dual Inline) [THT]"]

nets:
  N1: U1.D0, J1.pin2
  N2: U1.D1, LCM1602_IIC1.SCL
  N3: U1.D2, LCM1602_IIC1.SDA
  N4: U1.3V3, S1.Pin_3, S1.Pin_4, S2.Pin_3, S2.Pin_4, J1.pin1
  N5: U1.GND#6, U1.GND#13, U1.GND#16, U1.GND#33, R1.Pin_0, R2.Pin_0, LCM1602_IIC1.GND
  N6: U1.D5, S2.Pin_1, S2.Pin_2, R1.Pin_1
  N7: U1.D6, S1.Pin_1, S1.Pin_2, R2.Pin_1
  VIN: U1.Vin, LCM1602_IIC1.VCC
  VSS: LCD1.VSS, LCM1602_IIC1.VSS
  VDD: LCD1.VDD, LCM1602_IIC1.VDD
  N8: LCD1.V0, LCM1602_IIC1.V0
  N9: LCD1.RS, LCM1602_IIC1.RS
  N10: LCD1.R/W, LCM1602_IIC1.RW
  N11: LCD1.E, LCM1602_IIC1.E
  N12: LCD1.DB0, LCM1602_IIC1.D0
  N13: LCD1.DB1, LCM1602_IIC1.D1
  N14: LCD1.DB2, LCM1602_IIC1.D2
  N15: LCD1.DB3, LCM1602_IIC1.D3
  N16: LCD1.DB4, LCM1602_IIC1.D4
  N17: LCD1.DB5, LCM1602_IIC1.D5
  N18: LCD1.DB6, LCM1602_IIC1.D6
  N19: LCD1.DB7, LCM1602_IIC1.D7
  N20: LCD1.LED+, LCM1602_IIC1.A
  N21: LCD1.LED-, LCM1602_IIC1.K

custom parts:
  NodeMCU V3.0: ESP8266 based NodeMCU
  LCM1602 IIC: I2C-Module to use a 1602 or 2004 LCD on with the wire.h libory Serial LCD Modul
